# Fritzing sketch mine (saved by Fritzing 0.8.5b)
breadboards: 1

parts:
  Part1 = Pro Trinket 5V
  S1 = Momentary Switch [package=ksa_sealed_tac_switch]
  S2 = Momentary Switch [package=ksa_sealed_tac_switch]
  S3 = Momentary Switch [package=ksa_sealed_tac_switch]
  R1 = Resistor [tolerance=±5% resistance=220 package=THT]
  R2 = Resistor [tolerance=±5% resistance=220 package=THT]
  R3 = Resistor [tolerance=±5% resistance=220 package=THT]
  VCC1 = Battery
  U3 = 3.5mm Audio Jack [package=audio-jack-3.5mm-smd]
  U4 = 3.5mm Audio Jack [package=audio-jack-3.5mm-smd]

nets:
  N1: Part1.GND, R1.Pin_0, R2.Pin_0, R3.Pin_0, VCC1.-, U3.SLEEVE, U4.SLEEVE
  N2: Part1.VBAT, VCC1.+
  N3: Part1.D8, U3.RIGHT, U4.RIGHT
  N4: Part1.D6, S3.1
  N5: Part1.D5, S2.1
  N6: Part1.D4, S1.1
  N7: S1.4, R1.Pin_1
  N8: S2.4, R2.Pin_1
  N9: S3.4, R3.Pin_1
  N10: U3.LEFT, U4.LEFT

notes:
  I'm kind of surprised that I got anything started...

custom parts:
  Pro Trinket 5V: The Pro Trinket 5V is like an Arduino Pro Mini with more pins and USB included. Built with the common core Arduino chip, the ATmega328p, it has 18 GPIO, 2 extra analog inputs, 28K of flash, and 2K of RAM. It has onboard USB bootloading support with Optiboot support, so you can either program your Pro Trinket over USB or with a FTDI cable. The Pro Trinket is programmable using the Arduino IDE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
